// Logisim project Multiplicador Karatsuba circuitos combinacionais.circ as structural Verilog: 4 circuits, main circuit main
module main (
  input  [1:0] b,
  input  [1:0] c,
  output [3:0] out_3
);

  wire A_D_out, B_C_out, B_D_out;
  wire [0:0] A_C_out;
  wire [1:0] xor_1_out;
  wire [3:0] shifter_1_out, shifter_2_out;

  and A_C (A_C_out[0], b[1], c[1]);
  and B_D (B_D_out, c[0], b[0]);
  and A_D (A_D_out, b[1], c[0]);
  and B_C (B_C_out, b[0], c[1]);
  Shifter #(.width(4)) shifter_1 (.in({3'b000, A_C_out[0]}), .\dist (2'b10), .out(shifter_1_out));
  xor xor_1 (xor_1_out[0], A_D_out, B_C_out);
  and and_1 (xor_1_out[1], B_C_out, A_D_out);
  Shifter #(.width(4)) shifter_2 (.in({2'b00, xor_1_out}), .\dist (2'b01), .out(shifter_2_out));
  Adder #(.width(4)) adder_1 (.a(shifter_1_out), .b(shifter_2_out), .out(out_3), .cin(B_D_out));  // open: cout

  // Notes on the sheet:
  //   a
  //   d
endmodule

module Karatsuba_4bits (
  input  [3:0] in_1,
  input  [3:0] d,
  output [7:0] out_3
);

  wire [3:0] A_C_out_3, A_D_out_3, B_C_out_3, B_D_out_3;
  wire [7:0] adder_1_out, adder_2_out, bit_extender_1_out, bit_extender_2_out, bit_extender_3_out,
       bit_extender_4_out, shifter_1_out, shifter_2_out;

  main A_C (.b(in_1[3:2]), .c(d[3:2]), .out_3(A_C_out_3));
  main B_D (.b(in_1[1:0]), .c(d[1:0]), .out_3(B_D_out_3));
  main A_D (.b(in_1[3:2]), .c(d[1:0]), .out_3(A_D_out_3));
  main B_C (.b(in_1[1:0]), .c(d[3:2]), .out_3(B_C_out_3));
  assign bit_extender_1_out = {{4{1'b0}}, A_C_out_3};  // Bit_Extender bit_extender_1
  assign bit_extender_2_out = {{4{1'b0}}, A_D_out_3};  // Bit_Extender bit_extender_2
  assign bit_extender_3_out = {{4{1'b0}}, B_C_out_3};  // Bit_Extender bit_extender_3
  assign bit_extender_4_out = {{4{1'b0}}, B_D_out_3};  // Bit_Extender bit_extender_4
  Shifter shifter_1 (.in(bit_extender_1_out), .\dist (3'b100), .out(shifter_1_out));
  Adder adder_1 (.a(bit_extender_2_out), .b(bit_extender_3_out), .out(adder_1_out));  // open: cin, cout
  Shifter shifter_2 (.in(adder_1_out), .\dist (3'b010), .out(shifter_2_out));
  Adder adder_2 (.a(shifter_2_out), .b(shifter_1_out), .out(adder_2_out));  // open: cin, cout
  Adder adder_3 (.a(adder_2_out), .b(bit_extender_4_out), .out(out_3));  // open: cin, cout

  // Notes on the sheet:
  //   b
  //   a
  //   c
endmodule

module karatsuba_8bits (
  input  [7:0] in_1,
  input  [7:0] d,
  output [15:0] out_3
);

  wire [7:0] A_C_out_3, A_D_out_3, B_C_out_3, B_D_out_3;
  wire [15:0] adder_1_out, adder_2_out, bit_extender_1_out, bit_extender_2_out, bit_extender_3_out,
       bit_extender_4_out, shifter_1_out, shifter_2_out;

  Karatsuba_4bits A_C (.in_1(in_1[7:4]), .d(d[7:4]), .out_3(A_C_out_3));
  Karatsuba_4bits B_D (.in_1(in_1[3:0]), .d(d[3:0]), .out_3(B_D_out_3));
  Karatsuba_4bits A_D (.in_1(in_1[7:4]), .d(d[3:0]), .out_3(A_D_out_3));
  Karatsuba_4bits B_C (.in_1(in_1[3:0]), .d(d[7:4]), .out_3(B_C_out_3));
  assign bit_extender_1_out = {{8{1'b0}}, A_C_out_3};  // Bit_Extender bit_extender_1
  assign bit_extender_2_out = {{8{1'b0}}, A_D_out_3};  // Bit_Extender bit_extender_2
  assign bit_extender_3_out = {{8{1'b0}}, B_C_out_3};  // Bit_Extender bit_extender_3
  assign bit_extender_4_out = {{8{1'b0}}, B_D_out_3};  // Bit_Extender bit_extender_4
  Shifter #(.width(16)) shifter_1 (.in(bit_extender_1_out), .\dist (4'b1000), .out(shifter_1_out));
  Adder #(.width(16)) adder_1 (.a(bit_extender_2_out), .b(bit_extender_3_out), .out(adder_1_out));  // open: cin, cout
  Shifter #(.width(16)) shifter_2 (.in(adder_1_out), .\dist (4'b0100), .out(shifter_2_out));
  Adder #(.width(16)) adder_2 (.a(shifter_2_out), .b(shifter_1_out), .out(adder_2_out));  // open: cin, cout
  Adder #(.width(16)) adder_3 (.a(adder_2_out), .b(bit_extender_4_out), .out(out_3));  // open: cin, cout

  // Notes on the sheet:
  //   b
  //   a
  //   c
endmodule

module karatsuba_16_bits (
  input  [15:0] in_1,
  input  [15:0] d,
  output [31:0] out_3
);

  wire [15:0] A_C_out_3, A_D_out_3, B_C_out_3, B_D_out_3;
  wire [31:0] adder_1_out, adder_2_out, bit_extender_1_out, bit_extender_2_out, bit_extender_3_out,
       bit_extender_4_out, shifter_1_out, shifter_2_out;

  karatsuba_8bits A_C (.in_1(in_1[15:8]), .d(d[15:8]), .out_3(A_C_out_3));
  karatsuba_8bits B_D (.in_1(in_1[7:0]), .d(d[7:0]), .out_3(B_D_out_3));
  karatsuba_8bits A_D (.in_1(in_1[15:8]), .d(d[7:0]), .out_3(A_D_out_3));
  karatsuba_8bits B_C (.in_1(in_1[7:0]), .d(d[15:8]), .out_3(B_C_out_3));
  assign bit_extender_1_out = {{16{1'b0}}, A_C_out_3};  // Bit_Extender bit_extender_1
  assign bit_extender_2_out = {{16{1'b0}}, A_D_out_3};  // Bit_Extender bit_extender_2
  assign bit_extender_3_out = {{16{1'b0}}, B_C_out_3};  // Bit_Extender bit_extender_3
  assign bit_extender_4_out = {{16{1'b0}}, B_D_out_3};  // Bit_Extender bit_extender_4
  Shifter #(.width(32)) shifter_1 (.in(bit_extender_1_out), .\dist (5'b10000), .out(shifter_1_out));
  Adder #(.width(32)) adder_1 (.a(bit_extender_2_out), .b(bit_extender_3_out), .out(adder_1_out));  // open: cin, cout
  Shifter #(.width(32)) shifter_2 (.in(adder_1_out), .\dist (5'b01000), .out(shifter_2_out));
  Adder #(.width(32)) adder_2 (.a(shifter_2_out), .b(shifter_1_out), .out(adder_2_out));  // open: cin, cout
  Adder #(.width(32)) adder_3 (.a(adder_2_out), .b(bit_extender_4_out), .out(out_3));  // open: cin, cout

  // Notes on the sheet:
  //   b
  //   a
  //   c
endmodule
