// Logisim project karatsuba_modulo.circ as structural Verilog: 1 circuit, main circuit main
module main (
  input  [1:0] A,
  input  [1:0] B,
  output [3:0] out_3
);

  wire and_2_out, and_3_out, and_6_out, and_7_out, xor_1_out, xor_2_out;
  wire [0:0] and_4_out;
  wire [2:0] and_5_out;
  wire [2:2] and_1_out;
  wire [3:0] shifter_1_out, subtractor_1_out;

  and and_1 (and_1_out[2], B[1], A[1]);
  and and_2 (and_2_out, A[0], A[1]);
  and and_3 (and_3_out, B[0], B[1]);
  and and_4 (and_4_out[0], B[0], A[0]);
  xor xor_1 (xor_1_out, A[0], A[1]);
  xor xor_2 (xor_2_out, B[0], B[1]);
  and and_5 (and_5_out[0], xor_1_out, xor_2_out);
  and and_6 (and_6_out, and_2_out, xor_2_out);
  or or_1 (and_5_out[1], and_6_out, and_7_out);
  and and_7 (and_7_out, xor_1_out, and_3_out);
  and and_8 (and_5_out[2], and_2_out, and_3_out);
  Subtractor #(.width(4)) subtractor_1 (
    .a({1'b0, and_5_out}), .b({3'b000, and_4_out[0]}), .out(subtractor_1_out), .bin(and_1_out[2]));  // open: bout
  Shifter #(.width(4)) shifter_1 (.in(subtractor_1_out), .\dist (2'b01), .out(shifter_1_out));
  Adder #(.width(4)) adder_1 (
    .a(shifter_1_out), .b({1'b0, and_1_out[2], 2'b00}), .out(out_3), .cin(and_4_out[0]));  // open: cout
endmodule
